# Fritzing sketch Untitled Sketch (saved by Fritzing 0.9.3b)
breadboards: 1

parts:
  Componente1 = Arduino Nano (Rev3.0)
  Componente2 = HC-SR501 Body Sensor Module
  M2 = DC Motor
  M3 = DC Motor
  J1 = Piezo Speaker
  LED1 = LED - 5mm [color="Red (633nm)" package="5 mm [THT]"]  # not connected
  LED2 = LED - 5mm [color="Red (633nm)" package="5 mm [THT]"]  # not connected
  R1 = Resistor [tolerance=±5% resistance=470 package=THT]  # not connected
  R2 = Resistor [tolerance=±5% resistance=470 package=THT]  # not connected
  IC1 = IC, DIP package, 8 pins [chip_label=IC]  # not connected

nets:
  N1: Componente1.D9, J1.pin2
  GND: Componente1.GND, Componente2.GND, J1.pin1
  5V: Componente1.5V, Componente2.VCC
  N2: M2.pin_1, M3.pin_1
  N3: M2.pin_2, M3.pin_2

custom parts:
  HC-SR501 Body Sensor Module: Pyroelectric Infrared PIR Motion Sensor Detector Module
